# Fritzing sketch Bot-Power-Supply (saved by Fritzing 0.9.3b)
circuit board: 10.1732cm x 4.36622cm

parts:
  JPT-VOUT1 = Screw terminal - 2 pins [package=THT]
  JPT-VOUT2 = Screw terminal - 2 pins [package=THT]
  JPT-VBAT = Screw terminal - 2 pins [package=THT]
  JPH-UART = male pin header, 3 pins [form="♂ (male)"]
  JPH-VOUT1 = male pin header, 3 pins [form="♂ (male)"]
  JPH-VOUT2 = male pin header, 3 pins [form="♂ (male)"]
  MCU = Pro Trinket 5V
  ACS711EX1 = ACS711EX [part_number=2452 package="DIP (Dual Inline) [THT]"]
  LM2 = LM2596 3A DC-DC Step-Down Module [package="DIP (Dual Inline) [THT]"]
  LM3 = LM2596 3A DC-DC Step-Down Module [package="DIP (Dual Inline) [THT]"]
  JPT-VOUT3 = Screw terminal - 2 pins [package=THT]
  JPH-VOUT3 = male pin header, 3 pins [form="♂ (male)"]
  DFR1 = DFR0017 10A Relay Module [chip_label=DFR0017 package="DIP (Dual Inline) [THT]"]
  S1 = Toggle Switch [package=THT]
  LM4 = LM2596 3A DC-DC Step-Down Module [package="DIP (Dual Inline) [THT]"]
  JPT-VOUT4 = Screw terminal - 2 pins [package=THT]
  JPH-VOUT4 = male pin header, 3 pins [form="♂ (male)"]
  F1 = Resettable Fuse PTC [package=ptc]
  S2 = Toggle Switch [package=THT]
  S3 = Toggle Switch [package=THT]
  S4 = Toggle Switch [package=THT]

nets:
  VBAT: JPT-VOUT1.pin1, JPH-VOUT1.pin2, ACS711EX1.IP-, S2.L1, S3.L1, S4.L1
  GND: JPT-VOUT1.pin2, JPT-VOUT2.pin2, JPT-VBAT.pin2, JPH-UART.pin3, JPH-VOUT1.pin1, JPH-VOUT1.pin3, JPH-VOUT2.pin1, JPH-VOUT2.pin3, MCU.GND, ACS711EX1.GND, LM2.VIN-, LM2.VOUT-, LM3.VIN-, LM3.VOUT-, JPT-VOUT3.pin2, JPH-VOUT3.pin1, JPH-VOUT3.pin3, DFR1.GND, S1.L2, LM4.VIN-, LM4.VOUT-, JPT-VOUT4.pin2, JPH-VOUT4.pin1, JPH-VOUT4.pin3, S2.L2, S3.L2, S4.L2
  VOUT2: JPT-VOUT2.pin1, JPH-VOUT2.pin2, LM2.VOUT+
  N1: JPT-VBAT.pin1, F1.2
  N2: JPH-UART.pin1, MCU.RXD
  N3: JPH-UART.pin2, MCU.TXD
  VBAT-DIR: MCU.VBAT, MCU.A0, DFR1.COM, S1.COM
  5V: MCU.+5V, ACS711EX1.VCC, DFR1.VCC
  N4: MCU.D8, DFR1.IN
  N5: MCU.A1, ACS711EX1.OUT
  N6: ACS711EX1.IP+, DFR1.NO
  N7: LM2.VIN+, S2.COM
  N8: LM3.VIN+, S3.COM
  VOUT3: LM3.VOUT+, JPT-VOUT3.pin1, JPH-VOUT3.pin2
  N9: S1.L1, F1.1
  N10: LM4.VIN+, S4.COM
  VOUT4: LM4.VOUT+, JPT-VOUT4.pin1, JPH-VOUT4.pin2

custom parts:
  Pro Trinket 5V: The Pro Trinket 5V is like an Arduino Pro Mini with more pins and USB included. Built with the common core Arduino chip, the ATmega328p, it has 18 GPIO, 2 extra analog inputs, 28K of flash, and 2K of RAM. It has onboard USB bootloading support with Optiboot support, so you can either program your Pro Trinket over USB or with a FTDI cable. The Pro Trinket is programmable using the Arduino IDE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
  ACS711EX: A DIP stand-in part for whatever IC you want. With 10 pins on a 600mil dual inline package (DIP) footprint.
  LM2596 3A DC-DC Step-Down Module: A DIP stand-in part for whatever IC you want. With 4 pins on a 900mil dual inline package (DIP) footprint.
  DFR0017 10A Relay Module: Gravity: Relay Module V3.1
